# Fritzing sketch esp8266_Neopixel_PIR_Halloween (saved by Fritzing 0.9.3b)
breadboards: 1

parts:
  Bauteil1 = 12 NeoPixel Ring [part_number=1643]
  DFRobot_DFPlayer_Mini1 = DFRobot DFPlayer Mini [part_number=DFR0299]
  WeMos_D1_Mini1 = WeMos D1 Mini
  C1 = Electrolytic Capacitor [capacitance=1mF voltage=16V package="100 mil [THT, electrolytic]"]
  SPKR1 = Loudspeaker
  Breadboard_power_supply = Stromversorgung Breadboard [package=THT]
  PIR_motion_sensor = HC-SR501 Body Sensor Module
  R1 = Resistor [tolerance=±5% resistance=1k package=THT]

nets:
  N1: Bauteil1.IN, WeMos_D1_Mini1.RX
  VCC: Bauteil1.VDD, DFRobot_DFPlayer_Mini1.VCC, WeMos_D1_Mini1.5V, C1.+, Breadboard_power_supply.+5_/_+3_Volt_4#12, PIR_motion_sensor.VCC
  GND: Bauteil1.GND, DFRobot_DFPlayer_Mini1.GND-1, DFRobot_DFPlayer_Mini1.GND-2, WeMos_D1_Mini1.G, C1.-, Breadboard_power_supply.Ground_1, PIR_motion_sensor.GND
  N2: DFRobot_DFPlayer_Mini1.RX, R1.Pin_1
  N3: DFRobot_DFPlayer_Mini1.TX, WeMos_D1_Mini1.D2
  N4: DFRobot_DFPlayer_Mini1.SPK_1, SPKR1.pin2
  N5: DFRobot_DFPlayer_Mini1.SPK_2, SPKR1.pin1
  N6: WeMos_D1_Mini1.3V3, Breadboard_power_supply.+5_/_+3_Volt_4#13
  N7: WeMos_D1_Mini1.D1, R1.Pin_0
  N8: WeMos_D1_Mini1.D5, PIR_motion_sensor.OUT

notes:
  Voltage Supply: 3.3V + 5V
  DFPlayer: 1 kOhm Resistor to RxD
  NeoPixel: 1 mF Capacitor

custom parts:
  12 NeoPixel Ring: 12 ultra bright smart LED NeoPixels are arranged in a circle with 1.5" (37mm) outer diameter. The rings are 'chainable' - connect the output pin of one to the input pin of another. Use only one microcontroller pin to control as many as you can chain together! Each LED is addressable as the driver chip is inside the LED. Each one has ~18mA constant current drive so the color will be very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
  WeMos D1 Mini: The D1 mini is a mini wifi board based on ESP-8266EX.
  HC-SR501 Body Sensor Module: Pyroelectric Infrared PIR Motion Sensor Detector Module
